# Fritzing sketch fm transmitter (saved by Fritzing 1.0.1rc)
perfboards: 1
breadboards: 1

parts:
  Nano = Arduino Nano (Rev3.0)
  FM_transmitter = Si4713 Stereo FM Transmitter
  Nokia_5110_LCD_Module1 = Nokia 5110 LCD
  S1 = Momentary Switch [package=ksa_sealed_tac_switch]
  S2 = Momentary Switch [package=ksa_sealed_tac_switch]
  S3 = Momentary Switch [package=ksa_sealed_tac_switch]
  R1 = Resistor [tolerance=±5% power=0.25W resistance=1200 package=THT]
  R2 = Resistor [tolerance=±5% power=0.25W resistance=1200 package=THT]
  R3 = Resistor [tolerance=±5% power=0.25W resistance=1200 package=THT]
  Bat1 = battery_holder_single_18650
  U1 = SWITCH-SPST-2 [package=switch-spst-vertical]
  D1 = Rectifier Diode [part_number=1N5817 package="300 mil [THT]"]
  C1 = Electrolytic Capacitor [capacitance=3.3mF voltage=16V package="100 mil [THT, electrolytic]"]
  C2 = Electrolytic Capacitor [capacitance=3.3mF voltage=16V package="100 mil [THT, electrolytic]"]
  C3 = Electrolytic Capacitor [capacitance=3.3mF voltage=16V package="100 mil [THT, electrolytic]"]
  MOD1 = MT3608 Boost No usb
  Micro_USB = TP4056 [chip_label=TP4056 package="DIP (Dual Inline) [THT]"]
  C4 = Electrolytic Capacitor [capacitance=3.3mF voltage=35V package="100 mil [THT, electrolytic]"]
  C5 = Electrolytic Capacitor [capacitance=4.7mF voltage=35V package="100 mil [THT, electrolytic]"]

nets:
  GND: Nano.GND, FM_transmitter.GND, Nokia_5110_LCD_Module1.GND, R1.Pin_1, R2.Pin_1, R3.Pin_1, C1.-, C2.-, C3.-, MOD1.IN_(-), MOD1.OUT_(-), Micro_USB.pin6, C4.-, C5.-
  N1: Nano.D2, S1.4
  N2: Nano.D3, S2.4
  N3: Nano.D4, S3.4
  N4: Nano.D7, Nokia_5110_LCD_Module1.CLK
  N5: Nano.D8, Nokia_5110_LCD_Module1.Din
  N6: Nano.D9, Nokia_5110_LCD_Module1.D/C
  N7: Nano.D10, Nokia_5110_LCD_Module1.BL
  N8: Nano.D11/MOSI, Nokia_5110_LCD_Module1.CE
  N9: Nano.D12/MISO, Nokia_5110_LCD_Module1.RST
  N10: Nano.VIN, D1.cathode, C1.+, C2.+, C3.+
  N11: Nano.5V, S1.1, S2.1, S3.1
  N12: Nano.A5, FM_transmitter.SCL
  N13: Nano.A4, FM_transmitter.SDA
  3V3: Nano.3V3, FM_transmitter.VIN, Nokia_5110_LCD_Module1.VCC, C4.+, C5.+
  N14: Nano.D13/SCK, FM_transmitter.RST
  N15: S1.3, R1.Pin_0
  N16: S2.3, R2.Pin_0
  N17: S3.3, R3.Pin_0
  N18: Bat1.+#0, Micro_USB.pin5
  N19: Bat1.+#1, Micro_USB.pin4
  N20: U1.O, Micro_USB.pin3
  N21: U1.P, MOD1.IN_(+)
  N22: D1.anode, MOD1.OUT_(+)

custom parts:
  Si4713 Stereo FM Transmitter: Yaaar! Become your very own pirate radio station with this FM radio transmitter. This breakout board, based on the best-of-class Si4713, is an all-in-one stereo audio FM transmitter that can also transmit RDS/RBDS data!
  Nokia 5110 LCD: Nokia 5110 Graphic 84*48 LCD module <Blue Version>
  battery_holder_single_18650: single 18650 battery holder
  MT3608 Boost No usb: Chip- MT3608 / B6289 DC to DC step up, power booster module. With adjustable output voltage. Current- 2A . || Input voltage- 2V-24V || Output voltage- 5V-28V Input interface- Inversed polarity- NO. || Led indicator- No.
  TP4056: A DIP stand-in part for whatever IC you want. With 6 pins on a 300mil dual inline package (DIP) footprint.
